// Digital circuit 32_bit_adder.dig as structural Verilog
module _32_bit_adder (
  input  [31:0] A,
  input  [31:0] B,
  input  C_in,
  input  Mode,
  output C_out,
  output [31:0] S_out
);

  wire _4_bit_full_adder_2_c_out, _4_bit_full_adder_3_c_out, _4_bit_full_adder_4_c_out,
       _4_bit_full_adder_5_c_out, _4_bit_full_adder_6_c_out, _4_bit_full_adder_7_c_out,
       _4_bit_full_adder_8_c_out;
  wire [3:0] _4_bit_full_adder_1_s, _4_bit_full_adder_2_s, _4_bit_full_adder_3_s, _4_bit_full_adder_4_s,
       _4_bit_full_adder_5_s, _4_bit_full_adder_6_s, _4_bit_full_adder_7_s, _4_bit_full_adder_8_s,
       _32_bit_inverter_1_out, _32_bit_inverter_1_out_2, _32_bit_inverter_1_out_3, _32_bit_inverter_1_out_4,
       _32_bit_inverter_1_out_5, _32_bit_inverter_1_out_6, _32_bit_inverter_1_out_7, _32_bit_inverter_1_out_8;

  _32_bit_inverter _32_bit_inverter_1 (
    .Bit_s(A), .Mode(Mode),
    .Out({_32_bit_inverter_1_out_8, _32_bit_inverter_1_out_7, _32_bit_inverter_1_out_6, _32_bit_inverter_1_out_5, _32_bit_inverter_1_out_4, _32_bit_inverter_1_out_3, _32_bit_inverter_1_out_2, _32_bit_inverter_1_out}));
  _4_bit_full_adder _4_bit_full_adder_1 (
    .A(_32_bit_inverter_1_out_8), .B(B[31:28]), .C_in(_4_bit_full_adder_2_c_out), .C_out(C_out),
    .S(_4_bit_full_adder_1_s));
  _4_bit_full_adder _4_bit_full_adder_2 (
    .A(_32_bit_inverter_1_out_7), .B(B[27:24]), .C_in(_4_bit_full_adder_3_c_out),
    .C_out(_4_bit_full_adder_2_c_out), .S(_4_bit_full_adder_2_s));
  _4_bit_full_adder _4_bit_full_adder_3 (
    .A(_32_bit_inverter_1_out_6), .B(B[23:20]), .C_in(_4_bit_full_adder_4_c_out),
    .C_out(_4_bit_full_adder_3_c_out), .S(_4_bit_full_adder_3_s));
  _4_bit_full_adder _4_bit_full_adder_4 (
    .A(_32_bit_inverter_1_out_5), .B(B[19:16]), .C_in(_4_bit_full_adder_5_c_out),
    .C_out(_4_bit_full_adder_4_c_out), .S(_4_bit_full_adder_4_s));
  _4_bit_full_adder _4_bit_full_adder_5 (
    .A(_32_bit_inverter_1_out_4), .B(B[15:12]), .C_in(_4_bit_full_adder_6_c_out),
    .C_out(_4_bit_full_adder_5_c_out), .S(_4_bit_full_adder_5_s));
  _4_bit_full_adder _4_bit_full_adder_6 (
    .A(_32_bit_inverter_1_out_3), .B(B[11:8]), .C_in(_4_bit_full_adder_7_c_out),
    .C_out(_4_bit_full_adder_6_c_out), .S(_4_bit_full_adder_6_s));
  _4_bit_full_adder _4_bit_full_adder_7 (
    .A(_32_bit_inverter_1_out_2), .B(B[7:4]), .C_in(_4_bit_full_adder_8_c_out),
    .C_out(_4_bit_full_adder_7_c_out), .S(_4_bit_full_adder_7_s));
  _4_bit_full_adder _4_bit_full_adder_8 (
    .A(_32_bit_inverter_1_out), .B(B[3:0]), .C_in(C_in), .C_out(_4_bit_full_adder_8_c_out),
    .S(_4_bit_full_adder_8_s));
  _32_bit_inverter _32_bit_inverter_2 (
    .Bit_s({_4_bit_full_adder_1_s, _4_bit_full_adder_2_s, _4_bit_full_adder_3_s, _4_bit_full_adder_4_s, _4_bit_full_adder_5_s, _4_bit_full_adder_6_s, _4_bit_full_adder_7_s, _4_bit_full_adder_8_s}),
    .Mode(Mode), .Out(S_out));

  // Notes on the sheet:
  //   Mode: 0 for add, 1 for subtract
endmodule
