// Digital circuit 32_bit_inverter.dig as structural Verilog
module _32_bit_inverter (
  input  [31:0] Bit_s,
  input  Mode,
  output [31:0] Out
);

  assign Out = Bit_s ^ {32{Mode}};  // XOr xor_1, 32 bits wide

  // Notes on the sheet:
  //   Mode: 0 for on and 1 for off
endmodule
