// Digital circuit 4_bit_full_adder.dig as structural Verilog
module _4_bit_full_adder (
  input  [3:0] A,
  input  [3:0] B,
  input  C_in,
  output C_out,
  output [3:0] S
);

  wire full_adder_2_c_out, full_adder_3_c_out, full_adder_4_c_out;

  full_adder full_adder_1 (.a(A[3]), .b(B[3]), .c(full_adder_2_c_out), .S(S[3]), .C_out(C_out));
  full_adder full_adder_2 (.a(A[2]), .b(B[2]), .c(full_adder_3_c_out), .S(S[2]), .C_out(full_adder_2_c_out));
  full_adder full_adder_3 (.a(A[1]), .b(B[1]), .c(full_adder_4_c_out), .S(S[1]), .C_out(full_adder_3_c_out));
  full_adder full_adder_4 (.a(A[0]), .b(B[0]), .c(C_in), .S(S[0]), .C_out(full_adder_4_c_out));
endmodule
