// Digital circuit 4_bit_half_adder.dig as structural Verilog
module _4_bit_half_adder (
  input  in_5,
  input  in_6,
  input  in_7,
  input  in_8,
  input  in_9,
  input  in_10,
  input  in_12,
  input  in_13,
  output out_1,
  output out_2,
  output out_3,
  output out_4,
  output out_11
);

  wire full_adder_2_c_out, full_adder_3_c_out, half_adder_1_c;

  full_adder full_adder_1 (.a(in_13), .b(in_12), .c(full_adder_2_c_out), .S(out_4), .C_out(out_11));
  full_adder full_adder_2 (.a(in_5), .b(in_8), .c(full_adder_3_c_out), .S(out_3), .C_out(full_adder_2_c_out));
  full_adder full_adder_3 (.a(in_6), .b(in_9), .c(half_adder_1_c), .S(out_2), .C_out(full_adder_3_c_out));
  half_adder half_adder_1 (.a_1(in_7), .b_1(in_10), .o_1(out_1), .c(half_adder_1_c));
endmodule
