// Digital circuit 4_mode_32_bit_bitwise.dig as structural Verilog
module _4_mode_32_bit_bitwise (
  input  [1:0] Mode,
  input  [31:0] a_1,
  input  [31:0] a_2,
  output [31:0] Out
);

  wire [31:0] and_1_out, not_1_out, or_1_out, xor_1_out;

  assign xor_1_out = a_1 ^ a_2;  // XOr xor_1, 32 bits wide
  assign and_1_out = a_1 & a_2;  // And and_1, 32 bits wide
  assign or_1_out = a_1 | a_2;  // Or or_1, 32 bits wide
  assign not_1_out = ~a_1;  // Not not_1, 32 bits wide
  _4x_32_bit_switch _4x_32_bit_switch_1 (
    .Address(Mode), .p_0(xor_1_out), .p_1(and_1_out), .p_2(or_1_out), .p_3(not_1_out), .p_out(Out));
endmodule
