// Digital circuit 4x_32_bit_out_switch.dig as structural Verilog
module _4x_32_bit_out_switch (
  input  [1:0] addr,
  input  write,
  output out_0,
  output out_1,
  output out_2,
  output out_3
);

  wire and_1_out, and_2_out, and_3_out, and_4_out, not_1_out, not_2_out;

  not not_1 (not_1_out, addr[0]);
  not not_2 (not_2_out, addr[1]);
  and and_1 (and_1_out, not_2_out, not_1_out);
  and and_2 (and_2_out, not_2_out, addr[0]);
  and and_3 (and_3_out, addr[1], not_1_out);
  and and_4 (and_4_out, addr[1], addr[0]);
  and and_5 (out_0, and_1_out, write);
  and and_6 (out_1, and_2_out, write);
  and and_7 (out_2, and_3_out, write);
  and and_8 (out_3, and_4_out, write);
endmodule
