// Digital circuit 4x_32_bit_switch.dig as structural Verilog
module _4x_32_bit_switch (
  input  [1:0] Address,
  input  [31:0] p_0,
  input  [31:0] p_1,
  input  [31:0] p_2,
  input  [31:0] p_3,
  output [31:0] p_out
);

  wire and_1_out, and_2_out, and_3_out, and_4_out, not_1_out, not_2_out, not_3_out, not_4_out;
  wire [31:0] and_5_out, and_6_out, and_7_out, and_8_out, generic_multiplier_1_p2, generic_multiplier_2_p2,
       generic_multiplier_3_p2, generic_multiplier_4_p2;

  not not_1 (not_1_out, Address[0]);
  not not_2 (not_2_out, Address[1]);
  not not_3 (not_3_out, Address[1]);
  not not_4 (not_4_out, Address[0]);
  and and_1 (and_1_out, not_1_out, not_2_out);
  and and_2 (and_2_out, Address[0], not_3_out);
  and and_3 (and_3_out, not_4_out, Address[1]);
  and and_4 (and_4_out, Address[0], Address[1]);
  // generic_multiplier #(.generic("bitWidth := 32;")) generic_multiplier_1: pin names not known; wires that end beside it: and_1_out, generic_multiplier_1_p2
  // generic_multiplier #(.generic("bitWidth := 32;")) generic_multiplier_2: pin names not known; wires that end beside it: and_2_out, generic_multiplier_2_p2
  // generic_multiplier #(.generic("bitWidth := 32;")) generic_multiplier_3: pin names not known; wires that end beside it: and_3_out, generic_multiplier_3_p2
  // generic_multiplier #(.generic("bitWidth := 32;")) generic_multiplier_4: pin names not known; wires that end beside it: and_4_out, generic_multiplier_4_p2
  assign and_5_out = p_0 & generic_multiplier_1_p2;  // And and_5, 32 bits wide
  assign and_6_out = p_1 & generic_multiplier_2_p2;  // And and_6, 32 bits wide
  assign and_7_out = p_2 & generic_multiplier_3_p2;  // And and_7, 32 bits wide
  assign and_8_out = p_3 & generic_multiplier_4_p2;  // And and_8, 32 bits wide
  assign p_out = and_5_out | and_6_out | and_7_out | and_8_out;  // Or or_1, 32 bits wide
  // Probe on p_out
endmodule
