// Digital circuit 5_32_register_switch.dig as structural Verilog
module _5_32_register_switch (
  input  [31:0] In_1,
  input  [31:0] In_2,
  input  [31:0] In_3,
  input  [31:0] In_4,
  input  [31:0] In_5,
  input  [4:0] A,
  output [31:0] Out
);

  wire [31:0] and_1_out, and_2_out, and_3_out, and_4_out, and_5_out, generic_multiplier_1_p2,
       generic_multiplier_2_p2, generic_multiplier_3_p2, generic_multiplier_4_p2, generic_multiplier_5_p2;

  // generic_multiplier #(.generic("bitWidth := 32;")) generic_multiplier_1: pin names not known; wires that end beside it: A[0], generic_multiplier_1_p2
  // generic_multiplier #(.generic("bitWidth := 32;")) generic_multiplier_2: pin names not known; wires that end beside it: A[1], generic_multiplier_2_p2
  // generic_multiplier #(.generic("bitWidth := 32;")) generic_multiplier_3: pin names not known; wires that end beside it: A[2], generic_multiplier_3_p2
  // generic_multiplier #(.generic("bitWidth := 32;")) generic_multiplier_4: pin names not known; wires that end beside it: A[3], generic_multiplier_4_p2
  // generic_multiplier #(.generic("bitWidth := 32;")) generic_multiplier_5: pin names not known; wires that end beside it: A[4], generic_multiplier_5_p2
  assign and_1_out = In_1 & generic_multiplier_1_p2;  // And and_1, 32 bits wide
  assign and_2_out = In_2 & generic_multiplier_2_p2;  // And and_2, 32 bits wide
  assign and_3_out = In_3 & generic_multiplier_3_p2;  // And and_3, 32 bits wide
  assign and_4_out = In_4 & generic_multiplier_4_p2;  // And and_4, 32 bits wide
  assign and_5_out = In_5 & generic_multiplier_5_p2;  // And and_5, 32 bits wide
  assign Out = and_1_out | and_2_out | and_3_out | and_4_out | and_5_out;  // Or or_1, 32 bits wide
endmodule
