// Digital circuit computer.dig as structural Verilog
module computer (
  input  Clock,
  input  Clock_On,
  input  [31:0] p_0,
  input  [31:0] p_1,
  input  [31:0] p_2,
  input  [31:0] p_3,
  input  [63:0] Instruction,
  output [23:0] A_r,
  output [31:0] r_1,
  output [31:0] r_2,
  output [31:0] r_3,
  output [31:0] r_4,
  output [31:0] r_5,
  output [4:0] r_6,
  output pwrite_0,
  output pwrite_1,
  output pwrite_2,
  output pwrite_3,
  output [31:0] p_data
);

  wire _32_bit_adder_1_c_out, _32_bit_right_1_p2, and_1_out, and_2_out, generic_switch_1_out,
       generic_switch_2_out, generic_switch_3_out, generic_switch_4_out, generic_switch_5_out,
       generic_switch_7_out, or_1_out, or_2_out, or_3_out, Step_out;
  wire [1:0] generic_down_conversion_1_p2, generic_down_conversion_3_p1;
  wire [4:0] generic_down_conversion_2_p2;
  wire [31:0] _4_mode_32_bit_bitwise_1_out, _4x_32_bit_switch_1_p_out, _5_32_register_switch_1_out,
       _32_bit_adder_1_s_out, _32_bit_left_1_out, generic_switch_6_out, ramdualport_1_d;

  CounterPreset #(.Bits(24)) counterpreset_1 (
    .en(1'b1), .C(or_1_out), .dir(1'b0), .in(p_data[23:0]), .ld(or_2_out), .clr(Instruction[38]), .out(A_r));  // open: ovf
  and and_1 (and_1_out, Clock, Clock_On);
  Button Step (.out(Step_out));
  or or_1 (or_1_out, and_1_out, Step_out);
  or or_2 (or_2_out, and_2_out, Instruction[39]);
  Break break_1 (.brk(or_1_out));
  and and_2 (and_2_out, r_2[0], Instruction[47]);
  or or_3 (or_3_out, Instruction[44], Instruction[45]);
  generic_switch #(.generic("bitWidth := 32;")) generic_switch_1 (
    .A(Instruction[31:0]), .B(ramdualport_1_d), .C(Instruction[42]), .Out(generic_switch_1_out));
  Register #(.Bits(5)) register_1 (.D(generic_down_conversion_2_p2), .C(or_1_out), .en(Instruction[37]), .Q(r_6));
  generic_switch #(.generic("bitWidth := 32;")) generic_switch_2 (
    .A(generic_switch_1_out), .B(_5_32_register_switch_1_out), .C(Instruction[43]), .Out(generic_switch_2_out));
  generic_switch #(.generic("bitWidth := 32;")) generic_switch_3 (
    .A(generic_switch_2_out), .B(generic_switch_7_out), .C(or_3_out), .Out(generic_switch_3_out));
  generic_switch #(.generic("bitWidth := 32;")) generic_switch_4 (
    .A(generic_switch_3_out), .B(_32_bit_adder_1_s_out), .C(Instruction[46]), .Out(generic_switch_4_out));
  generic_switch #(.generic("bitWidth := 32;")) generic_switch_5 (
    .A(generic_switch_4_out), .B(_4x_32_bit_switch_1_p_out), .C(Instruction[48]), .Out(generic_switch_5_out));
  generic_switch #(.generic("bitWidth := 32;")) generic_switch_6 (
    .A(generic_switch_5_out), .B(_4_mode_32_bit_bitwise_1_out), .C(Instruction[41]),
    .Out(generic_switch_6_out));
  // generic_down_conversion #(.generic("InBits := 5; OutBits := 2;")) generic_down_conversion_1: pin names not known; wires that end beside it: r_6, generic_down_conversion_1_p2
  _4x_32_bit_switch _4x_32_bit_switch_1 (
    .Address(generic_down_conversion_1_p2), .p_0(p_0), .p_1(p_1), .p_2(p_2), .p_3(p_3),
    .p_out(_4x_32_bit_switch_1_p_out));
  _4x_32_bit_out_switch _4x_32_bit_out_switch_1 (
    .addr(generic_down_conversion_1_p2), .write(Instruction[49]), .out_0(pwrite_0), .out_1(pwrite_1),
    .out_2(pwrite_2), .out_3(pwrite_3));
  // generic_down_conversion #(.generic("InBits := 32; OutBits := 5;")) generic_down_conversion_2: pin names not known; wires that end beside it: generic_switch_6_out, generic_down_conversion_2_p2
  Register #(.Bits(32)) register_2 (.D(generic_switch_6_out), .C(or_1_out), .en(Instruction[32]), .Q(p_data));
  Register #(.Bits(32)) register_3 (.D(generic_switch_6_out), .C(or_1_out), .en(Instruction[33]), .Q(r_2));
  Register #(.Bits(32)) register_4 (.D(generic_switch_6_out), .C(or_1_out), .en(Instruction[34]), .Q(r_3));
  Register #(.Bits(32)) register_5 (.D(generic_switch_6_out), .C(or_1_out), .en(Instruction[35]), .Q(r_4));
  Register #(.Bits(32)) register_6 (.D(generic_switch_6_out), .C(or_1_out), .en(Instruction[36]), .Q(r_5));
  _32_bit_left _32_bit_left_1 (.in(p_data), .out(_32_bit_left_1_out));
  // _32_bit_right #(.generic("Bits := 32;")) _32_bit_right_1: pin names not known; wires that end beside it: p_data, _32_bit_right_1_p2
  _4_mode_32_bit_bitwise _4_mode_32_bit_bitwise_1 (
    .Mode(generic_down_conversion_3_p1), .a_1(p_data), .a_2(r_2), .Out(_4_mode_32_bit_bitwise_1_out));
  _5_32_register_switch _5_32_register_switch_1 (
    .In_1(p_data), .In_2(r_2), .In_3(r_3), .In_4(r_4), .In_5(r_5), .A(r_6), .Out(_5_32_register_switch_1_out));
  generic_switch #(.generic("bitWidth := 32;")) generic_switch_7 (
    .A(_32_bit_left_1_out), .B(_32_bit_right_1_p2), .C(Instruction[44]), .Out(generic_switch_7_out));
  // generic_down_conversion #(.generic("InBits := 32; OutBits := 2;")) generic_down_conversion_3: pin names not known; wires that end beside it: generic_down_conversion_3_p1, r_3
  // Probe Reg_3 on r_3[0]
  _32_bit_adder _32_bit_adder_1 (
    .A(p_data), .B(r_2), .C_in(1'b0), .Mode(r_3[0]), .C_out(_32_bit_adder_1_c_out),
    .S_out(_32_bit_adder_1_s_out));
  RAMDualPort #(.AddrBits(24), .Bits(32)) ramdualport_1 (
    .A(r_2[23:0]), .Din(p_data), .str(Instruction[40]), .C(or_1_out), .ld(Instruction[42]),
    .D(ramdualport_1_d));
  // Probe on _32_bit_adder_1_c_out
  // Probe Out on _32_bit_adder_1_s_out
  // Probe Out on ramdualport_1_d

  assign r_1 = p_data;

  // Notes on the sheet:
  //   Clock: Hz: 50
  //   A_r: ROM address
endmodule
