// Digital circuit 16_to_32_bit.dig as structural Verilog
module _16_to_32_bit (
  input  [15:0] In,
  output [31:0] Out
);


  assign Out = {{16{1'b0}}, In};

  // Notes on the sheet:
  //   In: Input
  //   Out: Output
endmodule
