// Digital circuit generic_multiplier.dig as structural Verilog
module generic_multiplier (
  input  In,
  output [62:0] Out
);


  assign Out = {63{In}};
endmodule

/* Code that sets the parameters or builds the circuit:
bitWidth := 32;
*/
