// Digital circuit full_adder.dig as structural Verilog
module full_adder (
  input  a,
  input  b,
  input  c,
  output S,
  output C_out
);

  wire and_1_out, half_adder_1_c, half_adder_1_o_1;

  half_adder half_adder_1 (.a_1(a), .b_1(b), .o_1(half_adder_1_o_1), .c(half_adder_1_c));
  xor xor_1 (S, half_adder_1_o_1, c);
  and and_1 (and_1_out, half_adder_1_o_1, c);
  or or_1 (C_out, and_1_out, half_adder_1_c);
endmodule
