// Digital circuit generic_bit_increaser.dig as structural Verilog
module generic_bit_increaser (
  input  [1:0] In,
  output [1:0] Out
);

  // Pins of 1 and 2 bits meet at {Out[1], In[0]}

  assign Out[0] = In[0];
endmodule

/* Code that sets the parameters or builds the circuit:
InBits := 32;
OutBits := 16;
*/
