// Digital circuit generic_register_shift.dig as structural Verilog
module generic_register_shift (
  input  A_in,
  input  B_in,
  input  [1:0] Flags_in,
  output A_out,
  output B_out,
  output Flags_out
);

  wire [62:0] generic_multiplier_1_out;

  // _32_bit_right #(.generic("Bits := args.Flags;")) _32_bit_right_1: pin names not known; wires that end beside it: Flags_in, Flags_out
  generic_multiplier #(.generic("bitWidth := args.Bits;")) generic_multiplier_1 (
    .In(Flags_in[0]), .Out(generic_multiplier_1_out));
  assign B_out = {63{B_in}} & generic_multiplier_1_out;  // And and_1, 63 bits wide
  assign A_out = {63{A_in}} & ~generic_multiplier_1_out;  // And and_2, 63 bits wide
endmodule

/* Code that sets the parameters or builds the circuit:
Bits := 4;
Flags := 4;
*/
