// Digital circuit generic_switch.dig as structural Verilog
module generic_switch (
  input  A,
  input  B,
  input  C,
  output Out
);

  wire and_1_out, and_2_out;
  wire [62:0] generic_multiplier_1_out;

  generic_multiplier #(.generic("bitWidth := args.bitWidth;")) generic_multiplier_1 (
    .In(C), .Out(generic_multiplier_1_out));
  assign and_1_out = {63{A}} & ~generic_multiplier_1_out;  // And and_1, 63 bits wide
  assign and_2_out = {63{B}} & generic_multiplier_1_out;  // And and_2, 63 bits wide
  or or_1 (Out, and_1_out, and_2_out);
endmodule

/* Code that sets the parameters or builds the circuit:
bitWidth := 32;
*/
