// Digital circuit 32_bit_right.dig as structural Verilog
module _32_bit_right (
  input  [31:0] in,
  output [31:0] out
);

  // Pins of 4 and 32 bits meet at in
  // Pins of 4 and 32 bits meet at {1'b0, in[31:1]}

  assign out = {1'b0, in[31:1]};
endmodule
