// Digital circuit system.dig as structural Verilog
module system (
  input  clk
);

  wire computer_1_pwrite_0, dipswitch_1_out, dipswitch_2_out;
  wire [4:0] computer_1_r_6;
  wire [23:0] computer_1_a_r;
  wire [31:0] computer_1_p_data, computer_1_r_1, computer_1_r_2, computer_1_r_3, computer_1_r_4,
       computer_1_r_5, register_1_q;
  wire [63:0] rom_1_d;

  ROM #(.AddrBits(24), .Bits(64)) rom_1 (.A(computer_1_a_r), .sel(dipswitch_1_out), .D(rom_1_d));
  DipSwitch #(.dipDefault("true")) dipswitch_1 (.out(dipswitch_1_out));
  Button button_1 ();  // open: out
  DipSwitch dipswitch_2 (.out(dipswitch_2_out));
  computer computer_1 (
    .Clock(clk), .Clock_On(dipswitch_2_out), .p_0(register_1_q), .p_1(32'h1), .p_2(32'h1), .p_3(32'h1),
    .Instruction(rom_1_d), .A_r(computer_1_a_r), .r_1(computer_1_r_1), .r_2(computer_1_r_2),
    .r_3(computer_1_r_3), .r_4(computer_1_r_4), .r_5(computer_1_r_5), .r_6(computer_1_r_6),
    .pwrite_0(computer_1_pwrite_0), .p_data(computer_1_p_data));  // open: pwrite_1, pwrite_2, pwrite_3
  // Probe on register_1_q
  Register #(.Bits(32)) register_1 (.D(computer_1_p_data), .C(clk), .en(computer_1_pwrite_0), .Q(register_1_q));
  // Probe on computer_1_p_data
  // Probe on computer_1_r_1
  // Probe on computer_1_r_2
  // Probe on computer_1_r_3
  // Probe on computer_1_r_4
  // Probe on computer_1_r_5
  // Probe on computer_1_r_6
  // Probe on computer_1_a_r

  // Notes on the sheet:
  //   clk: Hz: 50
  //   contents of rom_1 (hex, n*v repeats v):
  //   2000000000,200000001,0,1000100000000,400100000000,2000000000000
  //   ,100000002,8000000000,4000000000
endmodule
