// Digital circuit test.dig as structural Verilog
module test (
  input  Speed,
  input  in_2
);

  wire _32_bit_adder_1_c_out, and_1_out, button_1_out, or_1_out, or_2_out;
  wire [23:0] counterpreset_1_out, generic_switch_1_out, rom_1_d;
  wire [31:0] _32_bit_adder_1_s_out, ramdualport_1_d, register_1_q, register_2_q, register_3_q;
  wire [31:24] generic_switch_1_out_2;
  wire [63:24] rom_1_d_2;

  CounterPreset #(.Bits(24)) counterpreset_1 (
    .en(1'b1), .C(or_1_out), .dir(1'b0), .in(rom_1_d), .ld(rom_1_d_2[38]), .clr(rom_1_d_2[37]),
    .out(counterpreset_1_out));  // open: ovf
  and and_1 (and_1_out, Speed, in_2);
  Button button_1 (.out(button_1_out));
  // Probe Instruction on counterpreset_1_out
  ROM #(.AddrBits(24), .Bits(64)) rom_1 (.A(counterpreset_1_out), .sel(1'b1), .D({rom_1_d_2, rom_1_d}));
  or or_1 (or_1_out, and_1_out, button_1_out);
  generic_switch #(.generic("bitWidth := 32;")) generic_switch_1 (
    .A({rom_1_d_2[31:24], rom_1_d}), .B(ramdualport_1_d), .C(rom_1_d_2[41]),
    .Out({generic_switch_1_out_2, generic_switch_1_out}));
  or or_2 (or_2_out, rom_1_d_2[40], rom_1_d_2[41]);
  // Probe Clock on or_1_out
  Register #(.Bits(32)) register_1 (
    .D({generic_switch_1_out_2, generic_switch_1_out}), .C(or_1_out), .en(rom_1_d_2[32]), .Q(register_1_q));
  Register #(.Bits(32)) register_2 (
    .D({generic_switch_1_out_2, generic_switch_1_out}), .C(or_1_out), .en(rom_1_d_2[33]), .Q(register_2_q));
  Register #(.Bits(32)) register_3 (
    .D({generic_switch_1_out_2, generic_switch_1_out}), .C(or_1_out), .en(rom_1_d_2[34]), .Q(register_3_q));
  Register #(.Bits(32)) register_4 (
    .D({generic_switch_1_out_2, generic_switch_1_out}), .C(or_1_out), .en(rom_1_d_2[35]));  // open: Q
  Register #(.Bits(32)) register_5 (
    .D({generic_switch_1_out_2, generic_switch_1_out}), .C(or_1_out), .en(rom_1_d_2[36]));  // open: Q
  // Probe Reg_1 on register_1_q
  // Probe Reg_2 on register_2_q
  // Probe Reg_3 on register_3_q[0]
  _32_bit_adder _32_bit_adder_1 (
    .A(register_1_q), .B(register_2_q), .C_in(1'b0), .Mode(register_3_q[0]), .C_out(_32_bit_adder_1_c_out),
    .S_out(_32_bit_adder_1_s_out));
  RAMDualPort #(.AddrBits(24), .Bits(32)) ramdualport_1 (
    .A(generic_switch_1_out), .Din(register_1_q), .str(rom_1_d_2[39]), .C(or_1_out), .ld(or_2_out),
    .D(ramdualport_1_d));
  // Probe on _32_bit_adder_1_c_out
  // Probe Out on _32_bit_adder_1_s_out
  // Probe Out on ramdualport_1_d

  // Notes on the sheet:
  //   contents of rom_1 (hex, n*v repeats v):
  //   20000000a,10000000a,400000000a,10*0,8000000003,10000000003,2000000000
endmodule
